# Fritzing sketch rgb_remote_button (saved by Fritzing 0.9.3b)
breadboards: 1

parts:
  S1 = Pushbutton [package="[THT]"]
  LED2 = LED - 5mm [color="Green (570nm)" package="5 mm [THT]"]
  LED3 = LED - 5mm [color="Blue (525nm)" package="5 mm [THT]"]
  R1 = Resistor [tolerance=±5% resistance=220 package=THT]
  R2 = Resistor [tolerance=±5% resistance=220 package=THT]
  R3 = Resistor [tolerance=±5% resistance=220 package=THT]
  LED4 = RGB LED - (4 legs) [package="5 mm [THT]"]
  IR1 = TSOP312.., 314.. [package=THT]
  Part1 = Arduino Uno (Rev3)
  LED5 = LED - 5mm [color="Red (660nm)" package="5 mm [THT]"]
  R4 = Resistor [tolerance=±5% resistance=220 package=THT]
  R5 = Resistor [tolerance=±5% resistance=220 package=THT]
  R6 = Resistor [tolerance=±5% resistance=220 package=THT]

nets:
  GND: S1.Pin_1, S1.Pin_2, LED2.anode, LED3.anode, LED4.common_anode, IR1.GND, Part1.GND, LED5.anode
  N1: S1.Pin_3, S1.Pin_4, Part1.D8
  N2: LED2.cathode, R1.Pin_1
  N3: LED3.cathode, R2.Pin_1
  N4: R1.Pin_0, Part1.D11_PWM/MOSI
  N5: R2.Pin_0, Part1.D10_PWM/SS
  N6: R3.Pin_0, Part1.D12/MISO
  N7: R3.Pin_1, LED5.cathode
  N8: LED4.red_cathode, R6.Pin_1
  N9: LED4.green_cathode, R5.Pin_1
  N10: LED4.blue_cathode, R4.Pin_1
  N11: IR1.Vs, Part1.5V
  N12: IR1.Data, Part1.D3_PWM
  N13: Part1.D5_PWM, R4.Pin_0
  N14: Part1.D6_PWM, R5.Pin_0
  N15: Part1.D7, R6.Pin_0
